# Fritzing sketch RPi_Web_controled_Robot_Motors (saved by Fritzing 0.9.3b)
breadboards: 1

parts:
  Raspberry_Pi_1 = Raspberry Pi 3 [part_number=RPI-3-V1.2]
  IC3 = L293D [package=THT]
  LED1 = LED - 5mm [color="Red (660nm)" package="5 mm [THT]"]
  R1 = Resistor [tolerance=±5% resistance=220 package=THT]
  VCC1 = Battery block 9V
  M5 = DC Motor
  M6 = DC Motor
  C4 = Ceramic Capacitor [capacitance="100 nF" package="1206 [SMD, multilayer]"]
  C5 = Ceramic Capacitor [capacitance="100 nF" package="1206 [SMD, multilayer]"]
  C7 = Electrolytic Capacitor [capacitance=100μF package="0807 [SMD, electrolytic]"]
  C8 = Electrolytic Capacitor [capacitance=100μF package="0807 [SMD, electrolytic]"]

nets:
  N1: Raspberry_Pi_1.GIPO10, LED1.anode
  N2: Raspberry_Pi_1.GIPO5, IC3.In_4
  N3: Raspberry_Pi_1.GIPO6, IC3.In_3
  N4: Raspberry_Pi_1.GIPO13, IC3.In_1
  N5: Raspberry_Pi_1.GIPO19, IC3.In_2
  N6: Raspberry_Pi_1.GIPO18, IC3.Enable_1, IC3.Enable_2
  N7: Raspberry_Pi_1.GND, IC3.0V, R1.Pin_1, VCC1.-, C7.-, C8.-
  N8: Raspberry_Pi_1.5V, IC3.+V
  N9: IC3.Out_1_(_Controlled_by_Enable_1_), M5.pin_2, C4.1
  N10: IC3.Out_2_(_Controlled_by_Enable_1_), M5.pin_1, C4.0
  N11: IC3.+Vmotor, VCC1.+, C7.+
  N12: IC3.Out_3_(_Controlled_by_Enable_2_), M6.pin_2, C5.1
  N13: IC3.Out_4_(_Controlled_by_Enable_2_), M6.pin_1, C5.0
  N14: LED1.cathode, R1.Pin_0
